// Logisim project 4bit_by_3bit_divider.circ as structural Verilog: 1 circuit, main circuit main
module main (
);

  wire and_1_out, clock_1_out, nand_1_out, xnor_1_out, xnor_2_out, xnor_3_out, xnor_4_out, xnor_5_out,
       xnor_6_out, xnor_7_out;
  wire [2:0] counter_2_q, register_2_q;
  wire [3:0] counter_1_q, register_1_q;

  Register #(.width(4)) register_1 (.D(4'b1101), .Q(register_1_q), .clk(clock_1_out));  // open: en, clr
  Counter #(.width(4), .max('hf)) counter_1 (
    .count(nand_1_out), .Q(counter_1_q), .clk(clock_1_out));  // open: load, D, carry, clr
  Clock clock_1 (.out(clock_1_out));
  nand nand_1 (nand_1_out, xnor_4_out, xnor_3_out, xnor_2_out, xnor_1_out);
  xnor xnor_1 (xnor_1_out, register_1_q[3], counter_1_q[3]);
  xnor xnor_2 (xnor_2_out, register_1_q[2], counter_1_q[2]);
  xnor xnor_3 (xnor_3_out, register_1_q[1], counter_1_q[1]);
  xnor xnor_4 (xnor_4_out, register_1_q[0], counter_1_q[0]);
  Register #(.width(3)) register_2 (.D(3'b011), .Q(register_2_q), .clk(clock_1_out));  // open: en, clr
  Counter #(.width(3), .max('h7)) counter_2 (
    .count(nand_1_out), .Q(counter_2_q), .clk(clock_1_out), .clr(and_1_out));  // open: load, D, carry
  Counter counter_3 (.clk(and_1_out));  // open: load, D, count, Q, carry, clr
  and and_1 (and_1_out, xnor_7_out, xnor_6_out, xnor_5_out);
  xnor xnor_5 (xnor_5_out, register_2_q[2], counter_2_q[2]);
  xnor xnor_6 (xnor_6_out, register_2_q[1], counter_2_q[1]);
  xnor xnor_7 (xnor_7_out, register_2_q[0], counter_2_q[0]);

  // Notes on the sheet:
  //   4 bit by 3 bit divisor
  //   by Alissa Teigland
  //   dividend
  //   3 is MSB
  //   divisor
  //   remainder
  //   quotient
endmodule
