// Logisim project counts0to11.circ as structural Verilog: 1 circuit, main circuit main
module main (
);

  wire and_1_out, clock_1_out, d_ff_1_q, d_ff_1_qn, d_ff_2_q, d_ff_2_qn, d_ff_3_q, d_ff_3_qn, d_ff_4_qn;

  Clock clock_1 (.out(clock_1_out));
  and and_1 (and_1_out, d_ff_4_qn, d_ff_3_qn);
  D_Flip_Flop d_ff_1 (
    .clk(clock_1_out), .D(d_ff_1_qn), .Q(d_ff_1_q), .Qn(d_ff_1_qn), .preset(and_1_out));  // open: en, reset
  D_Flip_Flop d_ff_2 (
    .clk(d_ff_1_q), .D(d_ff_2_qn), .Q(d_ff_2_q), .Qn(d_ff_2_qn), .preset(and_1_out));  // open: en, reset
  D_Flip_Flop d_ff_3 (
    .clk(d_ff_2_q), .D(d_ff_3_qn), .Q(d_ff_3_q), .Qn(d_ff_3_qn), .preset(and_1_out));  // open: en, reset
  D_Flip_Flop d_ff_4 (.clk(d_ff_3_q), .D(d_ff_4_qn), .Qn(d_ff_4_qn), .preset(and_1_out));  // open: Q, en, reset
  LED led_1 (.in(d_ff_4_qn));
  LED led_2 (.in(d_ff_3_qn));
  LED led_3 (.in(d_ff_2_qn));
  LED led_4 (.in(d_ff_1_qn));
endmodule
